// Logisim project cpu.circ as structural Verilog: 41 circuits, main circuit main
module main (
  input  [31:0] INSTRUCTION,
  input  CLOCK,
  output [31:0] FETCH_ADDRESS,
  output [31:0] s0_Value,
  output [31:0] s1_Value,
  output [31:0] s2_Value,
  output [31:0] ra_Value,
  output [31:0] sp_Value
);

  wire ALUsrc, and_1_out, branch, comparator_6_eq, JUMP, main_1_p1, main_1_p2, main_1_p9, main_1_p19,
       memToReg, memWrite, PCsrc, regDest, regWrite, shamt, Zero;
  wire [2:0] bitadder_1_out;
  wire [3:0] ALUOP, \function ;
  wire [4:0] comparator_1_gt, multiplexer_4_out;
  wire [27:0] pc_4;
  wire [31:0] ALUresult, branchValue, main_1_p17, main_2_p5, multiplexer_1_out, multiplexer_2_out,
       multiplexer_5_out, multiplexer_6_out, RD2, result, shifter_1_out;
  wire [31:16] immediate, JUMPaddress;

  and u_PCsrc (PCsrc, branch, Zero);
  Adder #(.width(32)) adder_1 (.a(FETCH_ADDRESS), .b(32'h4), .out({JUMPaddress[31:28], pc_4}));  // open: cin, cout
  Shifter #(.width(32)) shifter_1 (.in({immediate, INSTRUCTION[15:0]}), .\dist (5'b00010), .out(shifter_1_out));
  Multiplexer #(.width(32)) multiplexer_1 (
    .in0({JUMPaddress[31:28], pc_4}), .in1(branchValue), .out(multiplexer_1_out), .sel(PCsrc));  // open: en
  Adder #(.width(32)) adder_2 (
    .a(shifter_1_out), .b({JUMPaddress[31:28], pc_4}), .out(branchValue));  // open: cin, cout
  Multiplexer #(.width(32)) multiplexer_2 (
    .in0(multiplexer_1_out),
    .in1({JUMPaddress[31:28], 2'b00, INSTRUCTION[25:21], JUMPaddress[20:16], INSTRUCTION[15:0]}),
    .out(multiplexer_2_out), .sel(JUMP));  // open: en
  Register #(.width(32)) PC (.D(multiplexer_2_out), .Q(FETCH_ADDRESS), .clk(CLOCK));  // open: en, clr
  Multiplexer #(.width(16)) multiplexer_3 (
    .in0({16{1'b0}}), .in1({16{1'b1}}), .out(immediate), .sel(INSTRUCTION[15]));  // open: en
  FuncCont funccont_1 (
    .a(INSTRUCTION[0]), .b(INSTRUCTION[1]), .c(INSTRUCTION[2]), .d(INSTRUCTION[3]), .e(INSTRUCTION[4]),
    .f(INSTRUCTION[5]), .funct0(\function [0]), .funct1(\function [1]), .funct2(\function [2]),
    .funct3(\function [3]));
  controlUnit CONTROL_UNIT (
    .g(INSTRUCTION[26]), .h(INSTRUCTION[27]), .x2(INSTRUCTION[28]), .x3(INSTRUCTION[29]),
    .x4(INSTRUCTION[30]), .x5(INSTRUCTION[31]), .regWrite(regWrite), .regDest(regDest), .ALUsrc(ALUsrc),
    .branch(branch), .memWrite(memWrite), .memToReg(memToReg), .ALUop0(ALUOP[0]), .ALUop1(ALUOP[1]),
    .ALUop2(ALUOP[2]), .ALUop3(ALUOP[3]), .jump(JUMP));
  Multiplexer #(.width(5)) multiplexer_4 (
    .in0(INSTRUCTION[20:16]), .in1(INSTRUCTION[15:11]), .out(multiplexer_4_out), .sel(regDest));  // open: en
  shamt shamt_1 (.aluop(\function ), .in_1(ALUOP), .shamt(shamt));
  // regfile_main main_1: pin names not known; wires that end beside it: main_1_p1, main_1_p2, main_1_p2, INSTRUCTION[25:21], INSTRUCTION[20:16], multiplexer_4_out, s0_Value, result, main_1_p9, s1_Value, regWrite, s2_Value, CLOCK, main_1_p9, ra_Value, sp_Value, main_1_p17, RD2, main_1_p19
  Multiplexer #(.width(32)) multiplexer_5 (
    .in0(RD2), .in1({immediate, INSTRUCTION[15:0]}), .out(multiplexer_5_out), .sel(ALUsrc));  // open: en
  Multiplexer #(.width(32)) multiplexer_6 (
    .in0(main_1_p17), .in1({{27{1'b0}}, INSTRUCTION[10:6]}), .out(multiplexer_6_out), .sel(shamt));  // open: en
  altALU altalu_1 (
    .X(multiplexer_6_out), .out(ALUresult), .Y(multiplexer_5_out), .Zero(Zero), .in_3(ALUOP),
    .in_4(\function ));
  Comparator #(.width(32)) comparator_1 (.a(s0_Value), .b({32{1'b0}}), .gt(comparator_1_gt[0]));  // open: eq, lt
  Comparator #(.width(32)) comparator_2 (.a(s1_Value), .b({32{1'b0}}), .gt(comparator_1_gt[1]));  // open: eq, lt
  Comparator #(.width(32)) comparator_3 (.a(s2_Value), .b({32{1'b0}}), .gt(comparator_1_gt[2]));  // open: eq, lt
  Comparator #(.width(32)) comparator_4 (.a(ra_Value), .b({32{1'b0}}), .gt(comparator_1_gt[3]));  // open: eq, lt
  Comparator #(.width(32)) comparator_5 (.a(sp_Value), .b({32{1'b0}}), .gt(comparator_1_gt[4]));  // open: eq, lt
  Comparator #(.width(4)) comparator_6 (.a(ALUOP), .b(4'b0101), .eq(comparator_6_eq));  // open: gt, lt
  BitAdder #(.width(5)) bitadder_1 (.in0(comparator_1_gt), .out(bitadder_1_out));
  and and_1 (and_1_out, comparator_6_eq, branch);
  IOdevice IOdevice (.in_1(bitadder_1_out));
  Multiplexer #(.width(32)) multiplexer_7 (.in1(ALUresult), .out(ra_Value), .sel(and_1_out));  // open: in0, en
  // mem_main main_2: pin names not known; wires that end beside it: ALUresult, RD2, memWrite, CLOCK, main_2_p5
  Multiplexer #(.width(32)) multiplexer_8 (.in0(ALUresult), .in1(main_2_p5), .out(result), .sel(memToReg));  // open: en

  // Other names for the same wires on the sheet: clk = CLOCK; immediate[15:0] = INSTRUCTION[15:0];
  //   JUMPaddress (some bits) = {INSTRUCTION[25:21], INSTRUCTION[15:0]}; shift[4:0] = INSTRUCTION[10:6];
  //   shiftext[4:0] = INSTRUCTION[10:6]; rd[4:0] = INSTRUCTION[15:11]; rs[4:0] = INSTRUCTION[25:21];
  //   pc_4[31:28] = JUMPaddress[31:28]; pc[31:0] = FETCH_ADDRESS; ra[31:0] = ra_Value; rt[4:0] = INSTRUCTION[20:16];
  //   s0[31:0] = s0_Value; s1[31:0] = s1_Value; s2[31:0] = s2_Value; sp[31:0] = sp_Value

  // Notes on the sheet:
  //   Output
  //   These are outputs/inputs from run.circ
  //   Inputs
  //   $rt
  //   SIGNED-EXT IMMEDIATE
  //   These are DEBUG/TEST outputs from your circuit.
  //   RegDest
endmodule

module IOdevice (
  input  [2:0] in_1
);

  wire comparator_1_eq, comparator_2_eq, comparator_3_eq, comparator_4_eq, comparator_5_eq, comparator_6_eq;

  Comparator #(.width(3)) comparator_1 (.a(in_1), .b(3'b000), .eq(comparator_1_eq));  // open: gt, lt
  Comparator #(.width(3)) comparator_2 (.a(in_1), .b(3'b001), .eq(comparator_2_eq));  // open: gt, lt
  Comparator #(.width(3)) comparator_3 (.a(in_1), .b(3'b010), .eq(comparator_3_eq));  // open: gt, lt
  Comparator #(.width(3)) comparator_4 (.a(in_1), .b(3'b011), .eq(comparator_4_eq));  // open: gt, lt
  Comparator #(.width(3)) comparator_5 (.a(in_1), .b(3'b100), .eq(comparator_5_eq));  // open: gt, lt
  Comparator #(.width(3)) comparator_6 (.a(in_1), .b(3'b101), .eq(comparator_6_eq));  // open: gt, lt
  _7_Segment_Display u_7_segment_display_1 (
    .f(comparator_1_eq), .a(comparator_1_eq), .b(comparator_1_eq), .e(comparator_1_eq), .d(comparator_1_eq),
    .c(comparator_1_eq));  // open: g, dp
  _7_Segment_Display u_7_segment_display_2 (.b(comparator_2_eq), .c(comparator_2_eq));  // open: g, f, a, e, d, dp
  _7_Segment_Display u_7_segment_display_3 (
    .g(comparator_3_eq), .a(comparator_3_eq), .b(comparator_3_eq), .e(comparator_3_eq), .d(comparator_3_eq));  // open: f, c, dp
  _7_Segment_Display u_7_segment_display_4 (
    .g(comparator_4_eq), .a(comparator_4_eq), .b(comparator_4_eq), .d(comparator_4_eq), .c(comparator_4_eq));  // open: f, e, dp
  _7_Segment_Display u_7_segment_display_5 (
    .g(comparator_5_eq), .f(comparator_5_eq), .b(comparator_5_eq), .c(comparator_5_eq));  // open: a, e, d, dp
  _7_Segment_Display u_7_segment_display_6 (
    .g(comparator_6_eq), .f(comparator_6_eq), .a(comparator_6_eq), .d(comparator_6_eq), .c(comparator_6_eq));  // open: b, e, dp
endmodule

module clz (
  input  [31:0] X,
  output [31:0] out
);

  wire [4:0] bitfinder_1_index;
  wire [31:0] bit_extender_1_out;

  BitFinder #(.width(32), .\type ("high1")) bitfinder_1 (.in(X), .index(bitfinder_1_index));  // open: found
  assign bit_extender_1_out = {{27{1'b0}}, bitfinder_1_index};  // Bit_Extender bit_extender_1
  Subtractor #(.width(32)) subtractor_1 (.a(32'h20), .b(bit_extender_1_out), .out(out));  // open: bin, bout
endmodule

module ADDu (
  input  [31:0] X,
  input  [31:0] Y,
  output [31:0] Result
);

  Adder #(.width(32)) adder_1 (.a(X), .b(Y), .out(Result));  // open: cin, cout
endmodule

module ADDi (
  input  [31:0] X,
  input  [31:0] imm,
  output overflow,
  output [31:0] Result
);

  wire comparator_1_gt, comparator_2_gt, comparator_3_gt, comparator_4_gt, comparator_5_gt,
       multiplexer_1_out, multiplexer_2_out;
  wire [31:0] adder_1_out, adder_2_out, adder_3_out, adder_4_out, adder_5_out, adder_6_out, adder_7_out,
       adder_8_out, adder_9_out, multiplexer_3_out, not_1_out, not_2_out, not_3_out, not_4_out;
  wire [31:31] multiplexer_4_out;

  assign not_1_out = ~X;  // NOT_Gate not_1, 32 bits wide
  assign not_2_out = ~imm;  // NOT_Gate not_2, 32 bits wide
  Comparator #(.width(1), .mode("unsigned")) comparator_1 (
    .a(imm[31]), .b(X[31]), .gt(comparator_1_gt));  // open: eq, lt
  assign not_3_out = ~X;  // NOT_Gate not_3, 32 bits wide
  Adder #(.width(32)) adder_1 (.a(not_1_out), .b(32'h1), .out(adder_1_out));  // open: cin, cout
  Adder #(.width(32)) adder_2 (.a(not_2_out), .b(32'h1), .out(adder_2_out));  // open: cin, cout
  assign not_4_out = ~imm;  // NOT_Gate not_4, 32 bits wide
  Comparator #(.width(32), .mode("unsigned")) comparator_2 (
    .a(adder_1_out), .b(imm), .gt(comparator_2_gt));  // open: eq, lt
  Comparator #(.width(32), .mode("unsigned")) comparator_3 (
    .a(X), .b(adder_2_out), .gt(comparator_3_gt));  // open: eq, lt
  Adder #(.width(32)) adder_3 (.a({1'b0, imm[30:0]}), .b({1'b0, X[30:0]}), .out(adder_3_out));  // open: cin, cout
  Adder #(.width(32)) adder_4 (.a({1'b0, X[30:0]}), .b({1'b0, imm[30:0]}), .out(adder_4_out));  // open: cin, cout
  Adder #(.width(32)) adder_5 (.a({1'b0, X[30:0]}), .b({1'b0, imm[30:0]}), .out(adder_5_out));  // open: cin, cout
  Adder #(.width(32)) adder_6 (.a({1'b0, X[30:0]}), .b({1'b0, imm[30:0]}), .out(adder_6_out));  // open: cin, cout
  Adder #(.width(32)) adder_7 (.a(not_3_out), .b(32'h1), .out(adder_7_out));  // open: cin, cout
  Adder #(.width(32)) adder_8 (.a(32'h1), .b(not_4_out), .out(adder_8_out));  // open: cin, cout
  Multiplexer multiplexer_1 (.in0(imm[31]), .in1(X[31]), .out(multiplexer_1_out), .sel(comparator_2_gt));  // open: en
  Multiplexer multiplexer_2 (.in0(X[31]), .in1(imm[31]), .out(multiplexer_2_out), .sel(comparator_3_gt));  // open: en
  Multiplexer #(.width(32)) multiplexer_3 (
    .in0(adder_3_out), .in1(adder_4_out), .out(multiplexer_3_out), .sel(comparator_1_gt));  // open: en
  Comparator #(.width(32), .mode("unsigned")) comparator_4 (
    .a(adder_5_out), .b(32'h7fffffff), .gt(comparator_4_gt));  // open: eq, lt
  Adder #(.width(32)) adder_9 (.a(adder_7_out), .b(adder_8_out), .out(adder_9_out));  // open: cin, cout
  Multiplexer multiplexer_4 (
    .in0(multiplexer_1_out), .in1(multiplexer_2_out), .out(multiplexer_4_out[31]), .sel(comparator_1_gt));  // open: en
  Comparator #(.width(32), .mode("unsigned")) comparator_5 (
    .a(adder_9_out), .b(32'h7fffffff), .gt(comparator_5_gt));  // open: eq, lt
  Multiplexer #(.select(3), .enable("false")) multiplexer_5 (
    .in0(comparator_4_gt), .in1(1'b0), .in2(1'b0), .in3(comparator_5_gt), .out(overflow),
    .sel({1'b0, X[31], imm[31]}));  // open: in4, in5, in6, in7
  Multiplexer #(.select(3), .width(32), .enable("false")) multiplexer_6 (
    .in0(adder_5_out), .in1({multiplexer_4_out[31], multiplexer_3_out[30:0]}),
    .in2({multiplexer_4_out[31], multiplexer_3_out[30:0]}), .in3(adder_6_out), .out(Result),
    .sel({1'b0, X[31], imm[31]}));  // open: in4, in5, in6, in7
endmodule

module SLTU (
  input  [31:0] X,
  input  [31:0] imm,
  output [31:0] \output 
);

  Comparator #(.width(32), .mode("unsigned")) comparator_1 (.a(X), .b(imm), .lt(\output [0]));  // open: gt, eq

  assign \output [31:1] = {31{1'b0}};
endmodule

module SLTi (
  input  [31:0] X,
  input  [31:0] imm,
  output [31:0] Result
);

  wire comparator_1_lt;

  Comparator #(.width(32)) comparator_1 (.a(X), .b(imm), .lt(comparator_1_lt));  // open: gt, eq
  assign Result = {{31{1'b0}}, comparator_1_lt};  // Bit_Extender bit_extender_1
endmodule

module ANDi (
  input  [31:0] X,
  input  [31:0] imm,
  output [31:0] Result
);

  assign Result = X & imm;  // AND_Gate and_1, 32 bits wide
endmodule

module Ori (
  input  [31:0] X,
  input  [31:0] imm,
  output [31:0] Result
);

  assign Result = X | imm;  // OR_Gate or_1, 32 bits wide
endmodule

module lui (
  input  [31:0] imm,
  output [31:0] Result
);


  assign Result = {imm[15:0], {16{1'b0}}};
endmodule

module lw (
  input  [31:0] X,
  input  [31:0] imm,
  output [31:0] memlocation
);

  Adder #(.width(32)) adder_1 (.a(X), .b(imm), .out(memlocation));  // open: cin, cout
endmodule

module sw (
  input  [31:0] X,
  input  [31:0] imm,
  output [31:0] memlocation
);

  Adder #(.width(32)) adder_1 (.a(X), .b(imm), .out(memlocation));  // open: cin, cout
endmodule

module beq (
  input  [31:0] X,
  input  [31:0] Y,
  output Zero
);

  Comparator #(.width(32), .mode("unsigned")) comparator_1 (.a(X), .b(Y), .eq(Zero));  // open: gt, lt
endmodule

module bne (
  input  [31:0] X,
  input  [31:0] Y,
  output Zero
);

  wire comparator_1_eq;

  Comparator #(.width(32), .mode("unsigned")) comparator_1 (.a(X), .b(Y), .eq(comparator_1_eq));  // open: gt, lt
  not not_1 (Zero, comparator_1_eq);
endmodule

module j (
  input  [25:0] address,
  input  [31:0] pc,
  output [31:0] newPC
);

  wire [27:0] adder_1_out;

  Adder #(.width(32)) adder_1 (.a(pc), .b(32'h4), .out({newPC[31:28], adder_1_out}));  // open: cin, cout

  assign newPC[27:0] = {address, 2'b00};
endmodule

module jr (
  input  [31:0] rs,
  output [31:0] newPc
);


  assign newPc = rs;
endmodule

module jal (
  input  [25:0] address,
  input  [31:0] pc,
  output [31:0] newPC,
  output [31:0] ra
);

  Adder #(.width(32)) adder_1 (.a(pc), .b(32'h4), .out({newPC[31:28], ra[27:0]}));  // open: cin, cout

  assign newPC[27:0] = {address, 2'b00};
  assign ra[31:28] = newPC[31:28];
endmodule

module controlUnit (
  input  g,
  input  h,
  input  x2,
  input  x3,
  input  x4,
  input  x5,
  output regWrite,
  output regDest,
  output ALUsrc,
  output branch,
  output memWrite,
  output memToReg,
  output ALUop0,
  output ALUop1,
  output ALUop2,
  output ALUop3,
  output jump
);

  wire and_1_out, and_2_out, and_3_out, and_4_out, and_5_out, and_6_out, and_7_out, and_8_out, and_9_out,
       and_10_out, and_11_out, and_12_out, and_13_out, and_14_out, and_15_out, and_16_out, and_17_out,
       and_18_out, and_19_out, and_20_out, and_21_out, and_22_out, and_25_out, and_26_out, and_27_out,
       and_28_out, and_29_out, and_30_out, and_31_out, and_32_out, and_33_out, and_34_out, and_35_out,
       and_36_out, and_37_out, and_38_out, and_39_out, and_40_out, and_41_out, and_42_out, and_43_out,
       and_44_out, and_45_out, and_46_out, not_1_out, not_2_out, not_3_out, not_4_out, not_5_out, not_6_out,
       not_7_out, not_8_out, not_9_out, not_10_out, not_11_out, not_12_out, not_13_out, not_14_out,
       not_15_out, not_16_out, not_17_out, not_18_out, not_19_out, not_20_out, not_21_out, not_22_out,
       not_23_out, not_24_out, not_25_out, not_26_out, not_27_out, not_28_out, not_29_out, not_30_out,
       not_31_out, not_32_out, not_33_out, not_34_out, not_35_out, not_36_out, not_37_out, not_38_out,
       not_39_out, not_40_out, not_41_out, not_42_out, not_43_out, not_44_out, not_45_out, not_46_out,
       not_47_out, not_48_out, not_49_out, not_50_out, not_51_out, not_52_out, not_53_out, not_54_out,
       not_55_out, not_56_out, not_57_out, not_58_out, not_59_out, not_60_out, not_61_out, not_62_out,
       not_63_out, not_64_out, not_65_out, not_66_out, not_67_out, not_68_out, not_69_out, not_70_out,
       not_71_out, not_72_out, not_73_out, not_74_out, not_75_out, not_76_out, not_77_out, not_78_out,
       not_79_out, not_80_out, not_81_out, not_82_out, not_83_out, not_84_out, not_85_out, not_86_out,
       not_87_out, not_88_out, not_89_out, not_90_out, not_91_out, not_92_out, not_93_out, not_94_out,
       not_95_out, not_96_out, not_97_out, not_98_out, not_99_out, not_100_out, not_101_out, not_102_out,
       not_103_out, not_104_out, not_105_out, not_106_out, not_107_out, not_108_out, not_109_out,
       not_110_out, not_111_out, not_112_out, not_113_out, not_114_out, not_115_out, not_116_out,
       not_117_out, not_118_out, not_119_out, not_120_out, not_121_out, not_122_out, not_123_out,
       not_124_out, not_125_out, not_126_out, not_127_out, not_128_out, not_129_out, not_130_out,
       not_131_out, not_132_out, not_133_out, not_134_out, not_135_out, not_136_out, not_137_out,
       not_138_out, not_139_out, not_140_out, not_141_out, not_142_out, not_143_out, not_144_out,
       not_145_out, not_146_out, not_147_out, not_148_out, not_149_out, not_150_out, not_151_out,
       not_152_out, not_153_out, not_154_out, not_155_out, not_156_out, not_157_out, not_158_out,
       not_159_out, not_160_out, not_161_out, not_162_out, not_163_out, not_164_out;

  not not_1 (not_1_out, h);
  not not_2 (not_2_out, x2);
  not not_3 (not_3_out, x4);
  not not_4 (not_4_out, x5);
  not not_5 (not_5_out, h);
  not not_6 (not_6_out, x4);
  not not_7 (not_7_out, x5);
  not not_8 (not_8_out, g);
  not not_9 (not_9_out, x2);
  not not_10 (not_10_out, x4);
  not not_11 (not_11_out, x4);
  not not_12 (not_12_out, x5);
  not not_13 (not_13_out, x2);
  not not_14 (not_14_out, x3);
  not not_15 (not_15_out, x4);
  not not_16 (not_16_out, g);
  not not_17 (not_17_out, x2);
  not not_18 (not_18_out, x4);
  not not_19 (not_19_out, x2);
  not not_20 (not_20_out, x4);
  not not_21 (not_21_out, g);
  not not_22 (not_22_out, h);
  not not_23 (not_23_out, x2);
  not not_24 (not_24_out, x3);
  not not_25 (not_25_out, x4);
  not not_26 (not_26_out, x5);
  not not_27 (not_27_out, h);
  not not_28 (not_28_out, x2);
  not not_29 (not_29_out, x4);
  not not_30 (not_30_out, x5);
  not not_31 (not_31_out, g);
  not not_32 (not_32_out, h);
  not not_33 (not_33_out, x2);
  not not_34 (not_34_out, x4);
  not not_35 (not_35_out, x5);
  not not_36 (not_36_out, x2);
  not not_37 (not_37_out, x3);
  not not_38 (not_38_out, x4);
  not not_39 (not_39_out, x5);
  not not_40 (not_40_out, g);
  not not_41 (not_41_out, x2);
  not not_42 (not_42_out, x3);
  not not_43 (not_43_out, x4);
  not not_44 (not_44_out, x5);
  not not_45 (not_45_out, x2);
  not not_46 (not_46_out, x4);
  not not_47 (not_47_out, x5);
  not not_48 (not_48_out, g);
  not not_49 (not_49_out, x2);
  not not_50 (not_50_out, x4);
  not not_51 (not_51_out, x5);
  not not_52 (not_52_out, g);
  not not_53 (not_53_out, h);
  not not_54 (not_54_out, x4);
  not not_55 (not_55_out, x5);
  not not_56 (not_56_out, h);
  not not_57 (not_57_out, x4);
  not not_58 (not_58_out, x5);
  not not_59 (not_59_out, x4);
  not not_60 (not_60_out, x5);
  not not_61 (not_61_out, x2);
  not not_62 (not_62_out, x3);
  not not_63 (not_63_out, x4);
  not not_64 (not_64_out, x2);
  not not_65 (not_65_out, x4);
  not not_66 (not_66_out, g);
  not not_67 (not_67_out, h);
  not not_68 (not_68_out, x3);
  not not_69 (not_69_out, x4);
  not not_70 (not_70_out, x5);
  not not_71 (not_71_out, h);
  not not_72 (not_72_out, x3);
  not not_73 (not_73_out, x4);
  not not_74 (not_74_out, x5);
  not not_75 (not_75_out, h);
  not not_76 (not_76_out, x2);
  not not_77 (not_77_out, x3);
  not not_78 (not_78_out, x4);
  not not_79 (not_79_out, x5);
  not not_80 (not_80_out, x2);
  not not_81 (not_81_out, x4);
  not not_82 (not_82_out, x2);
  not not_83 (not_83_out, x3);
  not not_84 (not_84_out, x4);
  not not_85 (not_85_out, h);
  not not_86 (not_86_out, x2);
  not not_87 (not_87_out, x4);
  not not_88 (not_88_out, x5);
  not not_89 (not_89_out, g);
  not not_90 (not_90_out, h);
  not not_91 (not_91_out, x3);
  not not_92 (not_92_out, x4);
  not not_93 (not_93_out, x5);
  not not_94 (not_94_out, x2);
  not not_95 (not_95_out, x4);
  not not_96 (not_96_out, x5);
  not not_97 (not_97_out, x2);
  not not_98 (not_98_out, x4);
  not not_99 (not_99_out, x2);
  not not_100 (not_100_out, x4);
  not not_101 (not_101_out, x5);
  not not_102 (not_102_out, g);
  not not_103 (not_103_out, x2);
  not not_104 (not_104_out, x4);
  not not_105 (not_105_out, x5);
  not not_106 (not_106_out, h);
  not not_107 (not_107_out, x3);
  not not_108 (not_108_out, x4);
  not not_109 (not_109_out, x5);
  not not_110 (not_110_out, x4);
  not not_111 (not_111_out, x5);
  not not_112 (not_112_out, g);
  not not_113 (not_113_out, h);
  not not_114 (not_114_out, x2);
  not not_115 (not_115_out, x4);
  not not_116 (not_116_out, x5);
  not not_117 (not_117_out, x2);
  not not_118 (not_118_out, x4);
  not not_119 (not_119_out, x5);
  not not_120 (not_120_out, g);
  not not_121 (not_121_out, x2);
  not not_122 (not_122_out, x4);
  not not_123 (not_123_out, x5);
  not not_124 (not_124_out, g);
  not not_125 (not_125_out, h);
  not not_126 (not_126_out, x4);
  not not_127 (not_127_out, x5);
  not not_128 (not_128_out, x2);
  not not_129 (not_129_out, x3);
  not not_130 (not_130_out, x4);
  not not_131 (not_131_out, h);
  not not_132 (not_132_out, x3);
  not not_133 (not_133_out, x4);
  not not_134 (not_134_out, x5);
  not not_135 (not_135_out, h);
  not not_136 (not_136_out, x2);
  not not_137 (not_137_out, x3);
  not not_138 (not_138_out, x4);
  not not_139 (not_139_out, x5);
  not not_140 (not_140_out, x2);
  not not_141 (not_141_out, x4);
  not not_142 (not_142_out, x5);
  not not_143 (not_143_out, g);
  not not_144 (not_144_out, x2);
  not not_145 (not_145_out, x4);
  not not_146 (not_146_out, x5);
  not not_147 (not_147_out, g);
  not not_148 (not_148_out, h);
  not not_149 (not_149_out, x4);
  not not_150 (not_150_out, x5);
  not not_151 (not_151_out, h);
  not not_152 (not_152_out, x4);
  not not_153 (not_153_out, x5);
  not not_154 (not_154_out, x4);
  not not_155 (not_155_out, x5);
  not not_156 (not_156_out, x2);
  not not_157 (not_157_out, x3);
  not not_158 (not_158_out, x4);
  not not_159 (not_159_out, x2);
  not not_160 (not_160_out, x4);
  not not_161 (not_161_out, x2);
  not not_162 (not_162_out, x3);
  not not_163 (not_163_out, x4);
  not not_164 (not_164_out, x5);
  and and_1 (and_1_out, not_1_out, not_2_out, not_3_out, not_4_out);
  and and_2 (and_2_out, not_5_out, x3, not_6_out, not_7_out);
  and and_3 (and_3_out, not_8_out, h, not_9_out, x3, not_10_out);
  and and_4 (and_4_out, g, x3, not_11_out, not_12_out);
  and and_5 (and_5_out, g, h, not_13_out, not_14_out, not_15_out);
  and and_6 (and_6_out, not_16_out, h, not_17_out, x3, not_18_out, x5);
  and and_7 (and_7_out, g, h, not_19_out, x3, not_20_out, x5);
  and and_8 (and_8_out, not_21_out, not_22_out, not_23_out, not_24_out, not_25_out, not_26_out);
  and and_9 (and_9_out, g, not_27_out, not_28_out, x3, not_29_out, not_30_out);
  and and_10 (and_10_out, not_31_out, not_32_out, not_33_out, x3, not_34_out, not_35_out);
  and and_11 (and_11_out, g, h, not_36_out, not_37_out, not_38_out, not_39_out);
  and and_12 (and_12_out, not_40_out, h, not_41_out, not_42_out, not_43_out, not_44_out);
  and and_13 (and_13_out, g, h, not_45_out, x3, not_46_out, not_47_out);
  and and_14 (and_14_out, not_48_out, h, not_49_out, x3, not_50_out, not_51_out);
  and and_15 (and_15_out, not_52_out, not_53_out, x2, x3, not_54_out, not_55_out);
  and and_16 (and_16_out, g, not_56_out, x2, x3, not_57_out, not_58_out);
  and and_17 (and_17_out, g, h, x2, x3, not_59_out, not_60_out);
  and and_18 (and_18_out, g, h, not_61_out, not_62_out, not_63_out, x5);
  and and_19 (and_19_out, g, h, not_64_out, x3, not_65_out, x5);
  and and_20 (and_20_out, not_66_out, not_67_out, x2, not_68_out, not_69_out, not_70_out);
  and and_21 (and_21_out, g, not_71_out, x2, not_72_out, not_73_out, not_74_out);
  and and_22 (and_22_out, g, not_75_out, not_76_out, not_77_out, not_78_out, not_79_out);
  and and_23 (memWrite, g, h, not_80_out, x3, not_81_out, x5);
  and and_24 (memToReg, g, h, not_82_out, not_83_out, not_84_out, x5);
  and and_25 (and_25_out, not_85_out, not_86_out, x3, not_87_out, not_88_out);
  and and_26 (and_26_out, not_89_out, not_90_out, x2, not_91_out, not_92_out, not_93_out);
  and and_27 (and_27_out, g, not_94_out, not_95_out, not_96_out);
  and and_28 (and_28_out, g, h, not_97_out, x3, not_98_out);
  and and_29 (and_29_out, not_99_out, x3, not_100_out, not_101_out);
  and and_30 (and_30_out, not_102_out, h, not_103_out, not_104_out, not_105_out);
  and and_31 (and_31_out, g, not_106_out, x2, not_107_out, not_108_out, not_109_out);
  and and_32 (and_32_out, g, h, x3, not_110_out, not_111_out);
  and and_33 (and_33_out, not_112_out, not_113_out, not_114_out, x3, not_115_out, not_116_out);
  and and_34 (and_34_out, g, h, not_117_out, x3, not_118_out, not_119_out);
  and and_35 (and_35_out, not_120_out, h, not_121_out, x3, not_122_out, not_123_out);
  and and_36 (and_36_out, not_124_out, not_125_out, x2, x3, not_126_out, not_127_out);
  and and_37 (and_37_out, g, h, not_128_out, not_129_out, not_130_out, x5);
  and and_38 (and_38_out, g, not_131_out, x2, not_132_out, not_133_out, not_134_out);
  and and_39 (and_39_out, g, not_135_out, not_136_out, not_137_out, not_138_out, not_139_out);
  and and_40 (and_40_out, g, h, not_140_out, x3, not_141_out, not_142_out);
  and and_41 (and_41_out, not_143_out, h, not_144_out, x3, not_145_out, not_146_out);
  and and_42 (and_42_out, not_147_out, not_148_out, x2, x3, not_149_out, not_150_out);
  and and_43 (and_43_out, g, not_151_out, x2, x3, not_152_out, not_153_out);
  and and_44 (and_44_out, g, h, x2, x3, not_154_out, not_155_out);
  and and_45 (and_45_out, g, h, not_156_out, not_157_out, not_158_out, x5);
  and and_46 (and_46_out, g, h, not_159_out, x3, not_160_out, x5);
  and and_47 (jump, h, not_161_out, not_162_out, not_163_out, not_164_out);
  or or_1 (regWrite, and_1_out, and_2_out, and_3_out, and_4_out, and_5_out);
  or or_2 (regDest, and_6_out, and_7_out, and_8_out);
  or or_3 (branch, and_20_out, and_21_out, and_22_out);
  or or_4 (ALUop0, and_25_out, and_26_out, and_27_out, and_28_out);
  or or_5 (ALUop1, and_29_out, and_30_out, and_31_out, and_32_out);
  or or_6 (ALUop2, and_33_out, and_34_out, and_35_out, and_36_out, and_37_out, and_38_out, and_39_out);
  or or_7 (ALUop3, and_40_out, and_41_out, and_42_out, and_43_out, and_44_out, and_45_out, and_46_out);
  or or_8 (ALUsrc, and_9_out, and_10_out, and_11_out, and_12_out, and_13_out, and_14_out, and_15_out, and_16_out, and_17_out, and_18_out, and_19_out);
endmodule

module sll (
  input  [31:0] in,
  output [31:0] Out
);


  assign Out = {in[30:0], 1'b0};
endmodule

module slltwo (
  input  [31:0] in,
  output [31:0] Out
);

  wire [31:0] sll_1_out;

  sll sll_1 (.in(in), .Out(sll_1_out));
  sll sll_2 (.in(sll_1_out), .Out(Out));
endmodule

module sllfour (
  input  [31:0] in,
  output [31:0] Out
);

  wire [31:0] slltwo_1_out;

  slltwo slltwo_1 (.in(in), .Out(slltwo_1_out));
  slltwo slltwo_2 (.in(slltwo_1_out), .Out(Out));
endmodule

module sllocho (
  input  [31:0] in,
  output [31:0] Out
);

  wire [31:0] sllfour_1_out;

  sllfour sllfour_1 (.in(in), .Out(sllfour_1_out));
  sllfour sllfour_2 (.in(sllfour_1_out), .Out(Out));
endmodule

module sll16 (
  input  [31:0] in,
  output [31:0] Out
);

  wire [31:0] sllocho_1_out;

  sllocho sllocho_1 (.in(in), .Out(sllocho_1_out));
  sllocho sllocho_2 (.in(sllocho_1_out), .Out(Out));
endmodule

module sll32 (
  input  [31:0] in,
  output [31:0] Out
);

  wire [31:0] sll16_1_out;

  sll16 sll16_1 (.in(in), .Out(sll16_1_out));
  sll16 sll16_2 (.in(sll16_1_out), .Out(Out));
endmodule

module SRL (
  input  [31:0] X,
  input  [31:0] Y,
  output [31:0] Out
);

  sllFINAL sllfinal_1 (
    .Y({Y[0], Y[1], Y[2], Y[3], Y[4], Y[5], Y[6], Y[7], Y[8], Y[9], Y[10], Y[11], Y[12], Y[13], Y[14], Y[15], Y[16], Y[17], Y[18], Y[19], Y[20], Y[21], Y[22], Y[23], Y[24], Y[25], Y[26], Y[27], Y[28], Y[29], Y[30], Y[31]}),
    .X(X),
    .Out({Out[0], Out[1], Out[2], Out[3], Out[4], Out[5], Out[6], Out[7], Out[8], Out[9], Out[10], Out[11], Out[12], Out[13], Out[14], Out[15], Out[16], Out[17], Out[18], Out[19], Out[20], Out[21], Out[22], Out[23], Out[24], Out[25], Out[26], Out[27], Out[28], Out[29], Out[30], Out[31]}));
endmodule

module sllFINAL (
  input  [31:0] Y,
  input  [31:0] X,
  output [31:0] Out
);

  wire [31:0] multiplexer_1_out, multiplexer_2_out, multiplexer_3_out, multiplexer_4_out, multiplexer_5_out,
       sll16_1_out, sll32_1_out, sll_1_out, sllfour_1_out, sllocho_1_out, slltwo_1_out;

  sll32 sll32_1 (.in(Y), .Out(sll32_1_out));
  Multiplexer #(.width(32)) multiplexer_1 (
    .in0(Y), .in1(sll32_1_out), .out(multiplexer_1_out), .sel(X[5]));  // open: en
  sll16 sll16_1 (.in(multiplexer_1_out), .Out(sll16_1_out));
  sllfour sllfour_1 (.in(multiplexer_4_out), .Out(sllfour_1_out));
  Multiplexer #(.width(32)) multiplexer_2 (
    .in0(multiplexer_1_out), .in1(sll16_1_out), .out(multiplexer_2_out), .sel(X[4]));  // open: en
  Multiplexer #(.width(32)) multiplexer_3 (
    .in0(multiplexer_4_out), .in1(sllfour_1_out), .out(multiplexer_3_out), .sel(X[2]));  // open: en
  sllocho sllocho_1 (.in(multiplexer_2_out), .Out(sllocho_1_out));
  slltwo slltwo_1 (.in(multiplexer_3_out), .Out(slltwo_1_out));
  Multiplexer #(.width(32)) multiplexer_4 (
    .in0(multiplexer_2_out), .in1(sllocho_1_out), .out(multiplexer_4_out), .sel(X[3]));  // open: en
  Multiplexer #(.width(32)) multiplexer_5 (
    .in0(multiplexer_3_out), .in1(slltwo_1_out), .out(multiplexer_5_out), .sel(X[1]));  // open: en
  sll sll_1 (.in(multiplexer_5_out), .Out(sll_1_out));
  Multiplexer #(.width(32)) multiplexer_6 (
    .in0(multiplexer_5_out), .in1(sll_1_out), .out(Out), .sel(X[0]));  // open: en
endmodule

module sra (
  input  [31:0] Y,
  output [31:0] Out
);


  assign Out = {{2{Y[31]}}, Y[30:1]};
endmodule

module sratwo (
  input  [31:0] in,
  output [31:0] Out
);

  wire [31:0] sra_1_out;

  sra sra_1 (.Y(in), .Out(sra_1_out));
  sra sra_2 (.Y(sra_1_out), .Out(Out));
endmodule

module srafour (
  input  [31:0] in,
  output [31:0] Out
);

  wire [31:0] sratwo_1_out;

  sratwo sratwo_1 (.in(in), .Out(sratwo_1_out));
  sratwo sratwo_2 (.in(sratwo_1_out), .Out(Out));
endmodule

module sraocho (
  input  [31:0] in,
  output [31:0] Out
);

  wire [31:0] srafour_1_out;

  srafour srafour_1 (.in(in), .Out(srafour_1_out));
  srafour srafour_2 (.in(srafour_1_out), .Out(Out));
endmodule

module sra16 (
  input  [31:0] in,
  output [31:0] Out
);

  wire [31:0] sraocho_1_out;

  sraocho sraocho_1 (.in(in), .Out(sraocho_1_out));
  sraocho sraocho_2 (.in(sraocho_1_out), .Out(Out));
endmodule

module sraFINAL (
  input  [31:0] Y,
  input  [31:0] X,
  output [31:0] Out
);

  wire [31:0] multiplexer_1_out, multiplexer_2_out, multiplexer_3_out, multiplexer_4_out, sra16_1_out,
       sra_1_out, srafour_1_out, sraocho_1_out, sratwo_1_out;

  sra16 sra16_1 (.in(Y), .Out(sra16_1_out));
  srafour srafour_1 (.in(multiplexer_3_out), .Out(srafour_1_out));
  Multiplexer #(.width(32)) multiplexer_1 (
    .in0(Y), .in1(sra16_1_out), .out(multiplexer_1_out), .sel(X[4]));  // open: en
  Multiplexer #(.width(32)) multiplexer_2 (
    .in0(multiplexer_3_out), .in1(srafour_1_out), .out(multiplexer_2_out), .sel(X[2]));  // open: en
  sraocho sraocho_1 (.in(multiplexer_1_out), .Out(sraocho_1_out));
  sratwo sratwo_1 (.in(multiplexer_2_out), .Out(sratwo_1_out));
  Multiplexer #(.width(32)) multiplexer_3 (
    .in0(multiplexer_1_out), .in1(sraocho_1_out), .out(multiplexer_3_out), .sel(X[3]));  // open: en
  Multiplexer #(.width(32)) multiplexer_4 (
    .in0(multiplexer_2_out), .in1(sratwo_1_out), .out(multiplexer_4_out), .sel(X[1]));  // open: en
  sra sra_1 (.Y(multiplexer_4_out), .Out(sra_1_out));
  Multiplexer #(.width(32)) multiplexer_5 (
    .in0(multiplexer_4_out), .in1(sra_1_out), .out(Out), .sel(X[0]));  // open: en
endmodule

module ADD (
  input  [31:0] X,
  input  [31:0] Y,
  output overflow,
  output [31:0] Result
);

  wire comparator_1_gt, comparator_2_gt, comparator_3_gt, comparator_4_gt, comparator_5_gt,
       multiplexer_1_out, multiplexer_2_out;
  wire [31:0] adder_1_out, adder_2_out, adder_3_out, adder_4_out, adder_5_out, adder_6_out, adder_7_out,
       adder_8_out, adder_9_out, multiplexer_3_out, not_1_out, not_2_out, not_3_out, not_4_out;
  wire [31:31] multiplexer_4_out;

  assign not_1_out = ~X;  // NOT_Gate not_1, 32 bits wide
  assign not_2_out = ~Y;  // NOT_Gate not_2, 32 bits wide
  Comparator #(.width(1), .mode("unsigned")) comparator_1 (.a(Y[31]), .b(X[31]), .gt(comparator_1_gt));  // open: eq, lt
  assign not_3_out = ~X;  // NOT_Gate not_3, 32 bits wide
  Adder #(.width(32)) adder_1 (.a(not_1_out), .b(32'h1), .out(adder_1_out));  // open: cin, cout
  Adder #(.width(32)) adder_2 (.a(not_2_out), .b(32'h1), .out(adder_2_out));  // open: cin, cout
  assign not_4_out = ~Y;  // NOT_Gate not_4, 32 bits wide
  Comparator #(.width(32), .mode("unsigned")) comparator_2 (
    .a(adder_1_out), .b(Y), .gt(comparator_2_gt));  // open: eq, lt
  Comparator #(.width(32), .mode("unsigned")) comparator_3 (
    .a(X), .b(adder_2_out), .gt(comparator_3_gt));  // open: eq, lt
  Adder #(.width(32)) adder_3 (.a({1'b0, Y[30:0]}), .b({1'b0, X[30:0]}), .out(adder_3_out));  // open: cin, cout
  Adder #(.width(32)) adder_4 (.a({1'b0, X[30:0]}), .b({1'b0, Y[30:0]}), .out(adder_4_out));  // open: cin, cout
  Adder #(.width(32)) adder_5 (.a({1'b0, X[30:0]}), .b({1'b0, Y[30:0]}), .out(adder_5_out));  // open: cin, cout
  Adder #(.width(32)) adder_6 (.a({1'b0, X[30:0]}), .b({1'b0, Y[30:0]}), .out(adder_6_out));  // open: cin, cout
  Adder #(.width(32)) adder_7 (.a(not_3_out), .b(32'h1), .out(adder_7_out));  // open: cin, cout
  Adder #(.width(32)) adder_8 (.a(32'h1), .b(not_4_out), .out(adder_8_out));  // open: cin, cout
  Multiplexer multiplexer_1 (.in0(Y[31]), .in1(X[31]), .out(multiplexer_1_out), .sel(comparator_2_gt));  // open: en
  Multiplexer multiplexer_2 (.in0(X[31]), .in1(Y[31]), .out(multiplexer_2_out), .sel(comparator_3_gt));  // open: en
  Multiplexer #(.width(32)) multiplexer_3 (
    .in0(adder_3_out), .in1(adder_4_out), .out(multiplexer_3_out), .sel(comparator_1_gt));  // open: en
  Comparator #(.width(32), .mode("unsigned")) comparator_4 (
    .a(adder_5_out), .b(32'h7fffffff), .gt(comparator_4_gt));  // open: eq, lt
  Adder #(.width(32)) adder_9 (.a(adder_7_out), .b(adder_8_out), .out(adder_9_out));  // open: cin, cout
  Multiplexer multiplexer_4 (
    .in0(multiplexer_1_out), .in1(multiplexer_2_out), .out(multiplexer_4_out[31]), .sel(comparator_1_gt));  // open: en
  Comparator #(.width(32), .mode("unsigned")) comparator_5 (
    .a(adder_9_out), .b(32'h7fffffff), .gt(comparator_5_gt));  // open: eq, lt
  Multiplexer #(.select(3), .enable("false")) multiplexer_5 (
    .in0(comparator_4_gt), .in1(1'b0), .in2(1'b0), .in3(comparator_5_gt), .out(overflow),
    .sel({1'b0, X[31], Y[31]}));  // open: in4, in5, in6, in7
  Multiplexer #(.select(3), .width(32), .enable("false")) multiplexer_6 (
    .in0(adder_5_out), .in1({multiplexer_4_out[31], multiplexer_3_out[30:0]}),
    .in2({multiplexer_4_out[31], multiplexer_3_out[30:0]}), .in3(adder_6_out), .out(Result),
    .sel({1'b0, X[31], Y[31]}));  // open: in4, in5, in6, in7

  // Notes on the sheet:
  //   SO +/+
  //   +/+
  //   SO -/-
  //   -/-
  //   +/- or -/+
endmodule

module \or  (
  input  [31:0] X,
  input  [31:0] Y,
  output [31:0] Result
);

  assign Result = X | Y;  // OR_Gate or_1, 32 bits wide
endmodule

module \xor  (
  input  [31:0] X,
  input  [31:0] Y,
  output [31:0] Result
);

  assign Result = X ^ Y;  // XOR_Gate xor_1, 32 bits wide
endmodule

module SLT (
  input  [31:0] X,
  input  [31:0] Y,
  output [31:0] Result
);

  Comparator #(.width(32)) comparator_1 (.a(X), .b(Y), .lt(Result[0]));  // open: gt, eq

  assign Result[31:1] = {31{1'b0}};
endmodule

module SLTu (
  input  [31:0] X,
  input  [31:0] Y,
  output [31:0] Result
);

  wire comparator_1_lt;

  Comparator #(.width(32), .mode("unsigned")) comparator_1 (.a(X), .b(Y), .lt(comparator_1_lt));  // open: gt, eq
  assign Result = {{31{1'b0}}, comparator_1_lt};  // Bit_Extender bit_extender_1
endmodule

module AND (
  input  [31:0] X,
  input  [31:0] Y,
  output [31:0] Result
);

  assign Result = X & Y;  // AND_Gate and_1, 32 bits wide
endmodule

module FuncCont (
  input  a,
  input  b,
  input  c,
  input  d,
  input  e,
  input  f,
  output funct0,
  output funct1,
  output funct2,
  output funct3
);

  wire and_1_out, and_2_out, and_3_out, and_4_out, and_5_out, and_6_out, and_7_out, and_8_out, not_1_out,
       not_2_out, not_3_out, not_4_out, not_5_out, not_6_out, not_7_out, not_8_out, not_9_out, not_10_out;

  not not_1 (not_1_out, a);
  not not_2 (not_2_out, c);
  not not_3 (not_3_out, d);
  not not_4 (not_4_out, f);
  not not_5 (not_5_out, a);
  not not_6 (not_6_out, d);
  not not_7 (not_7_out, a);
  not not_8 (not_8_out, c);
  not not_9 (not_9_out, b);
  not not_10 (not_10_out, c);
  and and_1 (and_1_out, not_1_out, not_2_out, not_3_out, f);
  and and_2 (and_2_out, d, not_4_out);
  and and_3 (and_3_out, not_5_out, b, not_6_out);
  and and_4 (and_4_out, a, d);
  and and_5 (and_5_out, a, c);
  and and_6 (and_6_out, not_7_out, not_8_out, f);
  and and_7 (and_7_out, a, b);
  and and_8 (and_8_out, a, not_9_out, not_10_out);
  or or_1 (funct0, and_1_out, and_2_out, and_3_out, and_4_out, and_5_out);
  or or_2 (funct1, and_6_out, and_7_out);
  or or_3 (funct2, d, and_8_out);

  assign funct3 = c;
endmodule

// ALU
module altALU (
  input  [31:0] X,
  input  [31:0] Y,
  input  [3:0] in_3,
  input  [3:0] in_4,
  output [31:0] out,
  output Zero
);

  wire beq_zero, bne_zero, comparator_1_eq;
  wire [31:0] Addi_result, ADDu_result, ANDi_result, lui_result, lw_memlocation, main_1_p4,
       multiplexer_2_out, Ori_result, SLTi_result, SLTU_output, sw_memlocation;

  ADDu ADDu (.X(Y), .Result(ADDu_result));  // open: Y
  ADDi Addi (.X(X), .imm(Y), .Result(Addi_result));  // open: overflow
  SLTU SLTU (.imm(Y), .X(X), .\output (SLTU_output));
  SLTi SLTi (.X(X), .imm(Y), .Result(SLTi_result));
  ANDi ANDi (.X(X), .imm(Y), .Result(ANDi_result));
  Ori Ori (.X(X), .imm(Y), .Result(Ori_result));
  lui lui (.imm(Y), .Result(lui_result));
  lw lw (.X(X), .imm(Y), .memlocation(lw_memlocation));
  sw sw (.X(X), .imm(Y), .memlocation(sw_memlocation));
  beq beq (.X(X), .Y(Y), .Zero(beq_zero));
  bne bne (.X(X), .Y(Y), .Zero(bne_zero));
  Multiplexer #(.select(4)) multiplexer_1 (
    .in0(1'b0), .in1(beq_zero), .in2(1'b0), .in3(1'b0), .in4(1'b0), .in5(1'b0), .in6(bne_zero), .in7(1'b0),
    .in8(1'b0), .in9(1'b0), .in10(1'b0), .in11(1'b0), .in12(1'b0), .in13(1'b0), .in14(1'b0), .in15(1'b0),
    .out(Zero), .sel(in_3));  // open: en
  Multiplexer #(.select(4), .width(32)) multiplexer_2 (
    .in3(ADDu_result), .in7(Addi_result), .in8(Ori_result), .in9(sw_memlocation), .in10(lui_result),
    .in12(ANDi_result), .in13(lw_memlocation), .in14(SLTi_result), .in15(SLTU_output),
    .out(multiplexer_2_out), .sel(in_3));  // open: in0, in1, in2, in4, in5, in6, in11, en
  Multiplexer #(.width(32)) multiplexer_3 (
    .in0(multiplexer_2_out), .in1(main_1_p4), .out(out), .sel(comparator_1_eq));  // open: en
  // alu_main main_1: pin names not known; wires that end beside it: X, Y, in_4, main_1_p4
  Comparator #(.width(4)) comparator_1 (.a(in_3), .b(4'b0000), .eq(comparator_1_eq));  // open: gt, lt

  // Other names for the same wires on the sheet: ALUop[3:0] = in_3; funct[3:0] = in_4
endmodule

module shamt (
  input  [3:0] in_1,
  input  [3:0] aluop,
  output shamt
);

  wire comparator_1_eq, comparator_2_eq, comparator_3_eq, comparator_4_eq, or_1_out;

  Comparator #(.width(4)) comparator_1 (.a(in_1), .b(4'b0000), .eq(comparator_1_eq));  // open: gt, lt
  Comparator #(.width(4)) comparator_2 (.a(in_1), .b(4'b0001), .eq(comparator_2_eq));  // open: gt, lt
  Comparator #(.width(4)) comparator_3 (.a(in_1), .b(4'b0010), .eq(comparator_3_eq));  // open: gt, lt
  Comparator #(.width(4)) comparator_4 (.a(aluop), .b(4'b0000), .eq(comparator_4_eq));  // open: gt, lt
  or or_1 (or_1_out, comparator_1_eq, comparator_2_eq, comparator_3_eq);
  and and_1 (shamt, or_1_out, comparator_4_eq);

  // Notes on the sheet:
  //   funct
endmodule
