// Logisim project IOdevice_test.circ as structural Verilog: 1 circuit, main circuit main
module main (
  output [31:0] s0_Value,
  output [31:0] s1_Value,
  output [31:0] s2_Value,
  output [31:0] ra_Value,
  output [31:0] sp_Value,
  output [31:0] Time_Step,
  output [31:0] Requested_Address,
  output [31:0] Requested_Instruction,
  output halt
);

  wire clock_1_out, comparator_7_eq, comparator_8_eq, comparator_9_eq, comparator_10_eq, comparator_11_eq,
       comparator_12_eq;
  wire [2:0] bitadder_1_out;
  wire [4:0] comparator_2_gt;

  Clock clock_1 (.out(clock_1_out));
  cpu_main main_1 (
    .INSTRUCTION(Requested_Instruction), .CLOCK(clock_1_out), .FETCH_ADDRESS(Requested_Address),
    .s0_Value(s0_Value), .s1_Value(s1_Value), .s2_Value(s2_Value), .ra_Value(ra_Value), .sp_Value(sp_Value));
  Counter #(.width(32), .max('hffffffff)) counter_1 (
    .Q(Time_Step), .clk(clock_1_out));  // open: load, D, count, carry, clr
  Comparator #(.width(32)) comparator_1 (.a(Time_Step), .b(32'h4), .eq(halt));  // open: gt, lt
  // Probe on Requested_Address
  Comparator #(.width(32)) comparator_2 (.a(s0_Value), .b({32{1'b0}}), .gt(comparator_2_gt[0]));  // open: eq, lt
  Comparator #(.width(32)) comparator_3 (.a(s1_Value), .b({32{1'b0}}), .gt(comparator_2_gt[1]));  // open: eq, lt
  Comparator #(.width(32)) comparator_4 (.a(s2_Value), .b({32{1'b0}}), .gt(comparator_2_gt[2]));  // open: eq, lt
  Comparator #(.width(32)) comparator_5 (.a(ra_Value), .b({32{1'b0}}), .gt(comparator_2_gt[3]));  // open: eq, lt
  Comparator #(.width(32)) comparator_6 (.a(sp_Value), .b({32{1'b0}}), .gt(comparator_2_gt[4]));  // open: eq, lt
  BitAdder #(.width(5)) bitadder_1 (.in0(comparator_2_gt), .out(bitadder_1_out));
  ROM #(.addrWidth(24), .dataWidth(32)) rom_1 (
    .addr(Requested_Address[25:2]), .data(Requested_Instruction));  // open: sel
  Comparator #(.width(3)) comparator_7 (.a(bitadder_1_out), .b(3'b000), .eq(comparator_7_eq));  // open: gt, lt
  Comparator #(.width(3)) comparator_8 (.a(bitadder_1_out), .b(3'b001), .eq(comparator_8_eq));  // open: gt, lt
  Comparator #(.width(3)) comparator_9 (.a(bitadder_1_out), .b(3'b010), .eq(comparator_9_eq));  // open: gt, lt
  Comparator #(.width(3)) comparator_10 (.a(bitadder_1_out), .b(3'b011), .eq(comparator_10_eq));  // open: gt, lt
  Comparator #(.width(3)) comparator_11 (.a(bitadder_1_out), .b(3'b100), .eq(comparator_11_eq));  // open: gt, lt
  Comparator #(.width(3)) comparator_12 (.a(bitadder_1_out), .b(3'b101), .eq(comparator_12_eq));  // open: gt, lt
  // Probe on Requested_Instruction
  _7_Segment_Display u_7_segment_display_1 (
    .f(comparator_7_eq), .a(comparator_7_eq), .b(comparator_7_eq), .e(comparator_7_eq), .d(comparator_7_eq),
    .c(comparator_7_eq));  // open: g, dp
  _7_Segment_Display u_7_segment_display_2 (.b(comparator_8_eq), .c(comparator_8_eq));  // open: g, f, a, e, d, dp
  _7_Segment_Display u_7_segment_display_3 (
    .g(comparator_9_eq), .a(comparator_9_eq), .b(comparator_9_eq), .e(comparator_9_eq), .d(comparator_9_eq));  // open: f, c, dp
  _7_Segment_Display u_7_segment_display_4 (
    .g(comparator_10_eq), .a(comparator_10_eq), .b(comparator_10_eq), .d(comparator_10_eq),
    .c(comparator_10_eq));  // open: f, e, dp
  _7_Segment_Display u_7_segment_display_5 (
    .g(comparator_11_eq), .f(comparator_11_eq), .b(comparator_11_eq), .c(comparator_11_eq));  // open: a, e, d, dp
  _7_Segment_Display u_7_segment_display_6 (
    .g(comparator_12_eq), .f(comparator_12_eq), .a(comparator_12_eq), .d(comparator_12_eq),
    .c(comparator_12_eq));  // open: b, e, dp

  // Other names for the same wires on the sheet: fetch_addr[31:0] = Requested_Address;
  //   Instruction[31:0] = Requested_Instruction; ra[31:0] = ra_Value; s0[31:0] = s0_Value; s1[31:0] = s1_Value;
  //   s2[31:0] = s2_Value; sp[31:0] = sp_Value

  // Notes on the sheet:
  //   YOUR CPU SHOULD FIT IN HERE!
  //   Instruction Memory
  //   contents of rom_1 (hex, n*v repeats v):
  //   20100001 20110002 2119020
endmodule
